// Logisim project battleship.circ as structural Verilog: 3 circuits, main circuit main
module main (
  input  [3:0] in_1,
  input  in_2,
  output out_3,
  output out_4,
  output out_5,
  output out_6,
  output out_7,
  output out_8,
  output out_9,
  output out_10
);

  // Encoder encoder_1: pin names not known; wires that end beside it: in_1, out_4, out_6
endmodule

module decodificador (
  input  A,
  input  B,
  output out_3,
  output out_4,
  output out_5,
  output out_6
);

  and and_1 (out_3, A, B);
  and and_2 (out_4, ~B, A);  // AND_Gate
  and and_3 (out_5, B, ~A);  // AND_Gate
  and and_4 (out_6, ~B, ~A);  // AND_Gate
endmodule

module Encoder (
  input  [3:0] Navio,
  output [3:0] out_2
);

  wire and_1_out, and_2_out, and_3_out, and_4_out, and_5_out, and_6_out;

  and and_1 (and_1_out, ~Navio[3], ~Navio[2], Navio[0]);  // AND_Gate
  and and_2 (and_2_out, ~Navio[3], Navio[2], ~Navio[0]);  // AND_Gate
  and and_3 (and_3_out, Navio[3], ~Navio[1], Navio[0]);  // AND_Gate
  and and_4 (and_4_out, Navio[3], Navio[1], ~Navio[0]);  // AND_Gate
  and and_5 (and_5_out, ~Navio[3], ~Navio[2], ~Navio[0]);  // AND_Gate
  and and_6 (and_6_out, ~Navio[3], Navio[2], Navio[0]);  // AND_Gate
  and and_7 (out_2[2], Navio[3], Navio[1], Navio[0]);
  and and_8 (out_2[3], Navio[3], Navio[2], ~Navio[1], ~Navio[0]);  // AND_Gate
  or or_1 (out_2[0], and_1_out, and_2_out, and_3_out, and_4_out);
  or or_2 (out_2[1], and_5_out, and_6_out);
endmodule
